# Fritzing sketch esquema_sem_resistor_10k (saved by Fritzing 0.9.3b)
breadboards: 1

parts:
  Componente1 = Arduino Uno (Rev3)
  S2 = Pushbutton [package="[THT]"]
  R2 = Resistor [tolerance=±5% resistance=220 package=THT]
  LED1 = smd LED [color="Red (633nm)" package="0603 [SMD]"]

nets:
  N1: Componente1.D10_PWM/SS, S2.Pin_3, S2.Pin_4
  N2: Componente1.GND, S2.Pin_1, S2.Pin_2, R2.Pin_1
  N3: Componente1.D4, LED1.anode
  N4: R2.Pin_0, LED1.cathode

notes:
  Basta usar pullup na declaração de input do botão e não precisa resitor de 10k
